# Fritzing sketch 20240309 (saved by Fritzing 1.0.2b)
breadboards: 3

parts:
  Bat1 = battery_holder_single_18650
  A1 = DHT22 module
  J1 = Wago 221-412
  J2 = Wago 221-412
  J4 = Wago 221-413
  J5 = Wago 221-413
  J3 = Wago 221-412
  J6 = Wago 221-412
  J7 = Wago 221-412
  J8 = Wago 221-412
  J10 = Wago 221-413
  M1 = DOIT Esp32 DevKit v1 (30 pins long, 11 pins width) [part_number=ESP32S-PIN30]
  C1 = Ceramic Capacitor [capacitance=10pF voltage=6.3V package="0805 [SMD, multilayer]"]
  R1 = Resistor [tolerance=±5% resistance=10k package="0805 [SMD]"]
  R2 = Resistor [tolerance=±5% resistance=10k package="0805 [SMD]"]
  R3 = Resistor [tolerance=±5% resistance=10k package="0805 [SMD]"]
  A2 = SparkFun RJ45 Breakout v11
  A3 = SparkFun RJ45 Breakout v11
  Bat2 = battery_holder_single_18650
  Súčiastka1 = BME280 Breakout
  A4 = SDB628
  J9 = Wago 221-413
  TP1 = TP4056 [chip_label=TP4056 package="DIP (Dual Inline) [THT]"]

nets:
  N1: Bat1.+#0, Bat2.+#0, TP1.pin5
  N2: Bat1.+#1, Bat2.+#1, TP1.pin4
  3V3: A1.+, J5.Pin_1, J5.Pin_2, J5.Pin_3, M1.3V3, M1.D18, M1.D19, C1.0, R1.Pin_1, R2.Pin_1, R3.Pin_1, Súčiastka1.3.3V, A4.Pin_5, J9.Pin_1, J9.Pin_2, J9.Pin_3
  N3: A1.Out, J3.Pin_1, J3.Pin_2, J8.Pin_1, J8.Pin_2, M1.D23
  GND: A1.-, J4.Pin_1, J4.Pin_2, J4.Pin_3, J10.Pin_1, J10.Pin_2, J10.Pin_3, M1.GND, C1.1, A2.Pin_3, A2.Pin_4, A3.Pin_5, Súčiastka1.GND, A4.Pin_4
  N4: J1.Pin_1, J1.Pin_2, J6.Pin_1, J6.Pin_2, M1.D22, Súčiastka1.SCK/SCL
  N5: J2.Pin_1, J2.Pin_2, J7.Pin_1, J7.Pin_2, M1.D21, Súčiastka1.SDI/SDA
  N6: M1.D15, R1.Pin_0, A3.Pin_4
  N7: M1.VP, R3.Pin_0, A2.Pin_5
  N8: M1.D34, R2.Pin_0, A2.Pin_6
  N9: A4.Pin_1, TP1.pin3
  N10: A4.Pin_3, TP1.pin6

custom parts:
  battery_holder_single_18650: single 18650 battery holder
  DHT22 module: DHT22 module. Pins VCC Data GND.
  Wago 221-412: Wago 221-412 2 position splicing connector 12AWG.
  Wago 221-413: Wago 221-413 3 position splicing connector 12AWG.
  DOIT Esp32 DevKit v1 (30 pins long, 11 pins width): The DOIT Esp32 DevKit v1 is one of the development board created by DOIT to evaluate the ESP-WROOM-32 module. It is based on the ESP32 microcontroller that boasts Wifi, Bluetooth, Ethernet and Low Power support all in a single chip. (vanepp) made breadboard work, adjusted pin numbering and labels and reduced size of schematic and cleaned up pcb. This chip is 30pins long (2 x15) and 11 pins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
  SparkFun RJ45 Breakout v11: SparkFun RJ45 Breakout v11 breakout board.
  SDB628: Boost buck regulator module.
  TP4056: A DIP stand-in part for whatever IC you want. With 6 pins on a 300mil dual inline package (DIP) footprint.
